# Fritzing sketch circuit (saved by Fritzing 0.9.4)
breadboards: 1

parts:
  LCD1 = LCD screen
  R1 = Resistor [tolerance=±5% resistance=220 package=THT]
  R2 = Resistor [tolerance=±5% resistance=220 package=THT]
  R3 = Resistor [tolerance=±5% resistance=220 package=THT]
  J1 = Basic Servo
  Part1 = Arduino Leonardo (Rev3b)
  LED1 = LED - 5mm [color="Red (633nm)" package="5 mm [THT]"]
  LED2 = LED - 5mm [color="Yellow (595nm)" package="5 mm [THT]"]
  LED3 = LED - 5mm [color="Green (555nm)" package="5 mm [THT]"]

nets:
  GND: LCD1.VSS, LCD1.R/W, J1.gnd, Part1.GND, LED1.cathode, LED2.cathode, LED3.cathode
  VDD: LCD1.VDD, LCD1.LED+, R1.Pin_1, R2.Pin_1, R3.Pin_1, J1.vcc, Part1.5V
  N1: LCD1.V0, Part1.D11_PWM
  N2: LCD1.RS, Part1.A5
  N3: LCD1.E, Part1.A4
  N4: LCD1.DB4, Part1.A3
  N5: LCD1.DB5, Part1.A2
  N6: LCD1.DB6, Part1.A1
  N7: LCD1.DB7, Part1.A0
  N8: R1.Pin_0, Part1.D3_PWM/SCL, Part1.SCL, LED1.anode
  N9: R2.Pin_0, Part1.D5_PWM, LED2.anode
  N10: R3.Pin_0, Part1.D6_PWM/A7, LED3.anode
  N11: J1.pulse, Part1.D10_PWM/A10
